// Logisim project sequential-logic.circ as structural Verilog
module rs_latch (
  input  r,
  input  s,
  output out,
  output not_out
);

  \nor  nor_1 (.a(r), .b(not_out), .out(out));
  \nor  nor_2 (.a(out), .b(s), .out(not_out));
endmodule

module d_latch (
  input  in,
  input  load,
  output out,
  output not_out
);

  wire and_1_out, and_2_out, not_1_output;

  \not  not_1 (.\input (in), .\output (not_1_output));
  \and  and_1 (.a(not_1_output), .b(load), .out(and_1_out));
  \and  and_2 (.a(in), .b(load), .out(and_2_out));
  rs_latch rs_latch_1 (.r(and_1_out), .s(and_2_out), .out(out), .not_out(not_out));

  // Notes on the sheet:
  //   reset
  //   set
endmodule

module d_latch_tmp (
  input  in_1,
  input  in_2,
  output out_3
);

  wire and_1_out, and_2_out, not_1_output;

  \not  not_1 (.\input (in_2), .\output (not_1_output));
  \and  and_1 (.a(in_1), .b(in_2), .out(and_1_out));
  \and  and_2 (.a(not_1_output), .b(out_3), .out(and_2_out));
  \or  or_1 (.a(and_1_out), .b(and_2_out), .out(out_3));
endmodule
